# Fritzing sketch wheatstone (saved by Fritzing 1.0.5)
breadboards: 1

parts:
  R1 = 12mm Trimmer Potentiometer (Large) [maximum_resistance=200 knob_status=75% power=0.5W package=THT]
  R2 = Resistor [tolerance=±5% power=0.25W resistance=220 package=THT]
  VM1 = Multimeter (DC Voltage)
  U1 = BATTERY-2 [package=battery-aa]
  U2 = BATTERY-2 [package=battery-aa]
  R3 = Resistor [tolerance=±5% power=0.25W resistance=220 package=THT]
  R6 = Resistor [tolerance=±5% power=0.25W resistance=220 package=THT]
  R7 = Resistor [tolerance=±5% power=0.25W resistance=220 package=THT]

nets:
  N1: R1.wiper, R6.Pin_0
  N2: R1.leg2, R2.Pin_0, U1.+1
  N3: R2.Pin_1, VM1.V_Probe, R3.Pin_0
  N4: VM1.COM_Probe, R6.Pin_1, R7.Pin_0
  N5: U1.-1, U1.-2, U2.+1, U2.+2
  N6: U2.-1, U2.-2, R3.Pin_1, R7.Pin_1

notes:
  change poti knob status and restart simulation
